// Logisim project logism-1.00.circ as structural Verilog: 1 circuit, main circuit main
module main (
  input  in_1,
  input  set_Hours,
  input  set_minutes,
  input  in_4,
  input  in_5,
  input  set_minutes_2,
  input  set_Hours_2,
  input  in_8,
  input  in_9
);

  wire and_1_out, and_2_out, and_3_out, and_4_out, and_5_out, and_6_out, and_7_out, clock_1_out, clock_2_out,
       comparator_1_eq, comparator_2_eq, comparator_3_eq, comparator_4_eq, comparator_5_eq, comparator_6_eq,
       comparator_7_eq, comparator_8_eq, comparator_9_eq, comparator_10_eq, comparator_11_eq,
       comparator_12_eq, comparator_13_eq, comparator_14_eq, comparator_15_eq, comparator_16_eq,
       comparator_17_eq, comparator_18_eq, comparator_19_eq, comparator_20_eq, multiplexer_1_out,
       multiplexer_2_out, multiplexer_3_out, multiplexer_4_out, multiplexer_5_out, multiplexer_6_out,
       multiplexer_7_out, multiplexer_8_out, not_1_out, or_1_out, or_2_out, or_3_out, or_4_out, or_5_out,
       or_6_out, or_7_out, or_8_out, or_9_out, or_10_out, or_11_out, or_12_out, or_13_out, or_14_out,
       or_15_out, t_ff_1_q;
  wire [3:0] counter_1_q, counter_2_q, counter_3_q, counter_4_q, counter_5_q, counter_6_q, counter_7_q,
       counter_8_q, counter_9_q, counter_10_q;

  or or_1 (or_1_out, multiplexer_2_out, and_1_out);
  T_Flip_Flop t_ff_1 (.T(1'b1), .clk(or_1_out), .Q(t_ff_1_q), .reset(in_5));  // open: Qn, preset
  Counter #(.max('hf), .width(4)) counter_1 (
    .Q(counter_1_q), .clk(comparator_6_eq), .clr(or_2_out));  // open: load, D, count, carry, up
  Comparator #(.width(4)) comparator_1 (.a(counter_1_q), .b(counter_5_q), .eq(comparator_1_eq));  // open: gt, lt
  Multiplexer multiplexer_1 (.in0(in_4), .in1(1'b0), .out(multiplexer_1_out), .sel(t_ff_1_q));
  Comparator #(.width(4)) comparator_2 (.a(4'b0010), .b(counter_1_q), .eq(comparator_2_eq));  // open: gt, lt
  Comparator #(.width(4)) comparator_3 (.a(4'b0001), .b(counter_1_q), .eq(comparator_3_eq));  // open: gt, lt
  or or_2 (or_2_out, in_5, or_4_out);
  Comparator #(.width(4)) comparator_4 (.a(4'b0101), .b(counter_2_q), .eq(comparator_4_eq));  // open: gt, lt
  Comparator #(.width(4)) comparator_5 (.a(4'b0011), .b(counter_2_q), .eq(comparator_5_eq));  // open: gt, lt
  Comparator #(.width(4)) comparator_6 (.a(4'b1010), .b(counter_2_q), .eq(comparator_6_eq));  // open: gt, lt
  Counter #(.max('hf), .width(4)) counter_2 (
    .Q(counter_2_q), .clk(or_5_out), .clr(or_3_out));  // open: load, D, count, carry, up
  or or_3 (or_3_out, comparator_6_eq, or_4_out);
  and and_1 (and_1_out, comparator_3_eq, comparator_5_eq);
  and and_2 (and_2_out, comparator_1_eq, comparator_7_eq);
  _7_Segment_Display u_7_segment_display_1 (
    .g(in_4), .f(in_4), .a(in_4), .b(in_4), .e(in_4), .c(multiplexer_1_out));  // open: d, dp
  and and_3 (and_3_out, comparator_4_eq, comparator_2_eq);
  or or_4 (or_4_out, multiplexer_3_out, in_5);
  Multiplexer multiplexer_2 (.in0(1'b0), .in1(in_8), .out(multiplexer_2_out), .sel(in_9));
  Comparator #(.width(4)) comparator_7 (.a(counter_2_q), .b(counter_7_q), .eq(comparator_7_eq));  // open: gt, lt
  LED led_1 (.in(in_4));
  Multiplexer multiplexer_3 (.in0(and_3_out), .in1(and_1_out), .out(multiplexer_3_out), .sel(in_4));
  or or_5 (or_5_out, or_6_out, multiplexer_4_out);
  LED led_2 (.in(not_1_out));
  not not_1 (not_1_out, in_4);
  Multiplexer multiplexer_4 (.in0(1'b0), .in1(set_Hours_2), .out(multiplexer_4_out), .sel(in_9));
  Counter #(.max('hf), .width(4)) counter_3 (
    .Q(counter_3_q), .clk(comparator_9_eq), .clr(or_6_out));  // open: load, D, count, carry, up
  or or_6 (or_6_out, comparator_8_eq, in_5);
  Comparator #(.width(4)) comparator_8 (.a(4'b0110), .b(counter_3_q), .eq(comparator_8_eq));  // open: gt, lt
  Counter #(.max('hf), .width(4)) counter_4 (
    .Q(counter_4_q), .clk(or_8_out), .clr(or_7_out));  // open: load, D, count, carry, up
  or or_7 (or_7_out, comparator_9_eq, in_5);
  Multiplexer multiplexer_5 (.in0(1'b0), .in1(set_minutes_2), .out(multiplexer_5_out), .sel(in_9));
  Counter #(.max('hf), .width(4)) counter_5 (
    .Q(counter_5_q), .clk(comparator_14_eq), .clr(or_9_out));  // open: load, D, count, carry, up
  Comparator #(.width(4)) comparator_9 (.a(4'b1010), .b(counter_4_q), .eq(comparator_9_eq));  // open: gt, lt
  or or_8 (or_8_out, or_11_out, multiplexer_5_out);
  Comparator #(.width(4)) comparator_10 (.a(4'b0010), .b(counter_5_q), .eq(comparator_10_eq));  // open: gt, lt
  Comparator #(.width(4)) comparator_11 (.a(4'b0001), .b(counter_5_q), .eq(comparator_11_eq));  // open: gt, lt
  or or_9 (or_9_out, in_1, or_12_out);
  Counter #(.max('hf), .width(4)) counter_6 (
    .Q(counter_6_q), .clk(comparator_16_eq), .clr(or_11_out));  // open: load, D, count, carry, up
  Comparator #(.width(4)) comparator_12 (.a(4'b0101), .b(counter_7_q), .eq(comparator_12_eq));  // open: gt, lt
  Comparator #(.width(4)) comparator_13 (.a(4'b0011), .b(counter_7_q), .eq(comparator_13_eq));  // open: gt, lt
  Comparator #(.width(4)) comparator_14 (.a(4'b1010), .b(counter_7_q), .eq(comparator_14_eq));  // open: gt, lt
  Counter #(.max('hf), .width(4)) counter_7 (
    .Q(counter_7_q), .clk(set_Hours), .clr(or_10_out));  // open: load, D, count, carry, up
  or or_10 (or_10_out, comparator_14_eq, or_12_out);
  Comparator #(.width(4)) comparator_15 (.a(4'b0110), .b(counter_6_q), .eq(comparator_15_eq));  // open: gt, lt
  or or_11 (or_11_out, comparator_15_eq, in_5);
  and and_4 (and_4_out, comparator_11_eq, comparator_13_eq);
  Counter #(.max('hf), .width(4)) counter_8 (
    .Q(counter_8_q), .clk(multiplexer_6_out), .clr(or_13_out));  // open: load, D, count, carry, up
  Clock clock_1 (.out(clock_1_out));
  and and_5 (and_5_out, comparator_12_eq, comparator_10_eq);
  or or_12 (or_12_out, multiplexer_8_out, in_1);
  Comparator #(.width(4)) comparator_16 (.a(4'b1010), .b(counter_8_q), .eq(comparator_16_eq));  // open: gt, lt
  or or_13 (or_13_out, comparator_16_eq, in_5);
  Multiplexer multiplexer_6 (.in0(clock_1_out), .in1(1'b1), .out(multiplexer_6_out), .sel(in_9));
  Clock clock_2 (.out(clock_2_out));
  Multiplexer multiplexer_7 (.in0(1'b0), .in1(clock_2_out), .out(multiplexer_7_out), .sel(and_6_out));
  LED led_3 (.in(multiplexer_7_out));
  Multiplexer multiplexer_8 (.in0(and_5_out), .in1(and_4_out), .out(multiplexer_8_out), .sel(in_4));
  Counter #(.max('hf), .width(4)) counter_9 (
    .Q(counter_9_q), .clk(comparator_20_eq), .clr(or_14_out));  // open: load, D, count, carry, up
  or or_14 (or_14_out, comparator_18_eq, in_1);
  Comparator #(.width(4)) comparator_17 (.a(counter_3_q), .b(counter_9_q), .eq(comparator_17_eq));  // open: gt, lt
  Comparator #(.width(4)) comparator_18 (.a(4'b0110), .b(counter_9_q), .eq(comparator_18_eq));  // open: gt, lt
  and and_6 (and_6_out, and_2_out, and_7_out);
  and and_7 (and_7_out, comparator_17_eq, comparator_19_eq);
  Counter #(.max('hf), .width(4)) counter_10 (
    .Q(counter_10_q), .clk(set_minutes), .clr(or_15_out));  // open: load, D, count, carry, up
  Comparator #(.width(4)) comparator_19 (.a(counter_4_q), .b(counter_10_q), .eq(comparator_19_eq));  // open: gt, lt
  Comparator #(.width(4)) comparator_20 (.a(4'b1010), .b(counter_10_q), .eq(comparator_20_eq));  // open: gt, lt
  or or_15 (or_15_out, comparator_20_eq, in_1);

  // Notes on the sheet:
  //   Reset button
  //   Set AM/PM
  //   hour format switch 
  //   12H
  //   24H
  //   Reset button
  //   set clock mode 
endmodule
